// Logisim project mct4.circ as structural Verilog: 2 circuits, main circuit main
module main (
  input  in_1,
  input  in_2,
  input  in_3,
  input  in_4,
  input  in_5,
  input  in_6
);

  wire button_1_out, button_2_out;
  wire [7:0] A_q, apu_1_sum, B_q, controlled_buffer_1_out, undriven;

  Button button_1 (.out(button_1_out));
  Button button_2 (.out(button_2_out));
  assign controlled_buffer_1_out = in_1 ? undriven : 8'bz;  // Controlled_Buffer controlled_buffer_1
  LedBar ledbar_1 (
    .led0(controlled_buffer_1_out[7]), .led1(controlled_buffer_1_out[6]), .led2(controlled_buffer_1_out[5]),
    .led3(controlled_buffer_1_out[4]), .led4(controlled_buffer_1_out[3]), .led5(controlled_buffer_1_out[2]),
    .led6(controlled_buffer_1_out[1]), .led7(controlled_buffer_1_out[0]));
  // DipSwitch dipswitch_1: pin names not known
  assign controlled_buffer_1_out = in_2 ? A_q : 8'bz;  // Controlled_Buffer controlled_buffer_2
  Register A (.D(controlled_buffer_1_out), .en(in_3), .clk(button_2_out), .Q(A_q), .clr(button_1_out));
  Register B (.D(controlled_buffer_1_out), .en(in_5), .clk(button_2_out), .Q(B_q), .clr(button_1_out));
  assign controlled_buffer_1_out = in_6 ? apu_1_sum : 8'bz;  // Controlled_Buffer controlled_buffer_3
  apu apu_1 (.A(A_q), .B(B_q), .AS(in_4), .sum(apu_1_sum));  // open: carry
endmodule

module apu (
  input  [7:0] A,
  input  [7:0] B,
  input  AS,
  output [7:0] sum,
  output carry
);

  wire adder_1_cout, subtractor_1_bout;
  wire [7:0] adder_1_out, subtractor_1_out;

  Adder adder_1 (.a(A), .b(B), .out(adder_1_out), .cout(adder_1_cout));  // open: cin
  Subtractor subtractor_1 (.a(A), .b(B), .out(subtractor_1_out), .bout(subtractor_1_bout));  // open: bin
  Multiplexer #(.width(8)) multiplexer_1 (.in0(adder_1_out), .in1(subtractor_1_out), .out(sum), .sel(AS));
  Multiplexer multiplexer_2 (.in0(adder_1_cout), .in1(subtractor_1_bout), .out(carry), .sel(AS));
endmodule
